// Logisim project N1_Processador_MIPS.circ as structural Verilog: 5 circuits, main circuit main
module main (
  output [17:0] out_1
);

  wire ALUSrc, Branch, button_1_out, choice, clock_1_out, Jump, MemRead, MemToReg, MemWrite, not_1_out,
       or_1_out, RegDst, RegWrite, ULA_igual;
  wire [1:0] ALUOp;
  wire [2:0] Controle_ULA_ulactrl, multiplexer_2_out;
  wire [7:0] adder_1_out, Banco_de_Registradores_read_data_1, conlRT, multiplexer_1_out, multiplexer_3_out,
       multiplexer_4_out, PC_q, ram_1_data, ULA_resultado;

  Clock clock_1 (.out(clock_1_out));
  Button button_1 (.out(button_1_out));
  Register PC (.D(multiplexer_1_out), .Q(PC_q), .clk(clock_1_out), .clr(button_1_out));  // open: en
  Adder adder_1 (.a(8'h1), .b(PC_q), .out(adder_1_out));  // open: cin, cout
  Multiplexer #(.width(8), .enable("false")) multiplexer_1 (
    .in0(adder_1_out), .in1(out_1[7:0]), .out(multiplexer_1_out), .sel(or_1_out));
  or or_1 (or_1_out, Jump, choice);
  ROM #(.dataWidth(18)) rom_1 (.addr(PC_q), .data(out_1));  // open: sel
  Multiplexer #(.width(3), .enable("false")) multiplexer_2 (
    .in0(out_1[11:9]), .in1(out_1[8:6]), .out(multiplexer_2_out), .sel(RegDst));
  unidade_de_controle unidade_de_controle_1 (
    .opcode(out_1[17:15]), .RegDst(RegDst), .RegWrite(RegWrite), .ALUSrc(ALUSrc), .MemWrite(MemWrite),
    .MemRead(MemRead), .MemToReg(MemToReg), .Branch(Branch), .Jump(Jump), .ALUOp(ALUOp));
  Banco_de_Registradores Banco_de_Registradores (
    .Read_Register_1(out_1[14:12]), .Read_Register_2(out_1[11:9]), .Write_Data(multiplexer_4_out),
    .Reg_Write(RegWrite), .Write_Register(multiplexer_2_out), .CLOCK(clock_1_out), .CLEAR(button_1_out),
    .Read_Data_1(Banco_de_Registradores_read_data_1), .Read_Data_2(conlRT));
  Multiplexer #(.width(8), .enable("false")) multiplexer_3 (
    .in0(conlRT), .in1(out_1[7:0]), .out(multiplexer_3_out), .sel(ALUSrc));
  Controle_ULA Controle_ULA (.FuncT(out_1[2:0]), .ALUOp(ALUOp), .ULACtrl(Controle_ULA_ulactrl));
  ULA ULA (
    .A(Banco_de_Registradores_read_data_1), .B(multiplexer_3_out), .Shamt(out_1[5:3]),
    .\Função (Controle_ULA_ulactrl), .Resultado(ULA_resultado), .IGUAL(ULA_igual));
  and and_1 (choice, Branch, ULA_igual);
  Multiplexer #(.width(8), .enable("false")) multiplexer_4 (
    .in0(ram_1_data), .in1(ULA_resultado), .out(multiplexer_4_out), .sel(MemToReg));
  RAM #(.bus("separate")) ram_1 (
    .addr(ULA_resultado), .din(conlRT), .data(ram_1_data), .str(MemWrite), .clk(not_1_out), .ld(MemRead),
    .clr(button_1_out));  // open: sel
  not not_1 (not_1_out, clock_1_out);

  // Other names for the same wires on the sheet: Address_imm[7:0] = out_1[7:0]; funct[2:0] = out_1[2:0];
  //   rd[2:0] = out_1[8:6]; rs[2:0] = out_1[14:12]; rt[2:0] = out_1[11:9]; shamt[2:0] = out_1[5:3];
  //   Upcode[2:0] = out_1[17:15]

  // Notes on the sheet:
  //   Memória de Instruções
  //   contents of rom_1 (hex, n*v repeats v):
  //   38001 20a08 0 20e08 20203 0 20205 0 20204 0 20201 20300 20207 4000 20207 20500 20208 20600 20205
  //   20700 20c00 20800 4a45 1901d 7840 20000 6380 24801 38016 6b83 20100 3801f
  //   Memórida de Dados
endmodule

module Banco_de_Registradores (
  input  [2:0] Read_Register_1,
  input  [2:0] Read_Register_2,
  input  [7:0] Write_Data,
  input  Reg_Write,
  input  [2:0] Write_Register,
  input  CLOCK,
  input  CLEAR,
  output [7:0] Read_Data_1,
  output [7:0] Read_Data_2
);

  wire Enable0, Enable1, Enable2, Enable3, Enable4, Enable5, Enable6, Enable7;
  wire [7:0] Reg0, Reg1, Reg2, Reg3, Reg4, Reg5, Reg6, Reg7, WReg0, WReg1, WReg2, WReg3, WReg4, WReg5, WReg6,
       WReg7;

  Demultiplexer #(.select(3), .width(8), .enable("false")) demultiplexer_1 (
    .out0(WReg0), .out1(WReg1), .out2(WReg2), .out3(WReg3), .out4(WReg4), .out5(WReg5), .out6(WReg6),
    .out7(WReg7), .in(Write_Data), .sel(Write_Register));
  Demultiplexer #(.select(3), .enable("false")) demultiplexer_2 (
    .out0(Enable0), .out1(Enable1), .out2(Enable2), .out3(Enable3), .out4(Enable4), .out5(Enable5),
    .out6(Enable6), .out7(Enable7), .in(Reg_Write), .sel(Write_Register));
  Register u_Reg0 (.D(WReg0), .en(Enable0), .Q(Reg0), .clk(CLOCK), .clr(CLEAR));
  Register u_Reg1 (.D(WReg1), .en(Enable1), .Q(Reg1), .clk(CLOCK), .clr(CLEAR));
  Register u_Reg2 (.D(WReg2), .en(Enable2), .Q(Reg2), .clk(CLOCK), .clr(CLEAR));
  Register u_Reg3 (.D(WReg3), .en(Enable3), .Q(Reg3), .clk(CLOCK), .clr(CLEAR));
  Register u_Reg4 (.D(WReg4), .en(Enable4), .Q(Reg4), .clk(CLOCK), .clr(CLEAR));
  Register u_Reg5 (.D(WReg5), .en(Enable5), .Q(Reg5), .clk(CLOCK), .clr(CLEAR));
  Register u_Reg6 (.D(WReg6), .en(Enable6), .Q(Reg6), .clk(CLOCK), .clr(CLEAR));
  Register u_Reg7 (.D(WReg7), .en(Enable7), .Q(Reg7), .clk(CLOCK), .clr(CLEAR));
  Multiplexer #(.select(3), .width(8)) multiplexer_1 (
    .in0(Reg0), .in1(Reg1), .in2(Reg2), .in3(Reg3), .in4(Reg4), .in5(Reg5), .in6(Reg6), .in7(Reg7),
    .out(Read_Data_1), .sel(Read_Register_1));  // open: en
  Multiplexer #(.select(3), .width(8)) multiplexer_2 (
    .in0(Reg0), .in1(Reg1), .in2(Reg2), .in3(Reg3), .in4(Reg4), .in5(Reg5), .in6(Reg6), .in7(Reg7),
    .out(Read_Data_2), .sel(Read_Register_2));  // open: en

  // Other names for the same wires on the sheet: Read_Reg1[2:0] = Read_Register_1; Read_Reg2[2:0] = Read_Register_2
endmodule

module ULA (
  input  [7:0] A,
  input  [7:0] B,
  input  [2:0] Shamt,
  input  [2:0] \Função ,
  output [7:0] Resultado,
  output IGUAL
);

  wire comparator_1_lt;
  wire [7:0] A_Comp, A_Div, A_Mult, A_Neg, A_ShiftDir, A_ShiftEsq, A_soma, A_Sub, adder_1_out, B_Comp, B_Div,
       B_Mult, B_soma, B_Sub, bit_extender_1_out, divider_1_out, multiplier_1_out, negator_1_out,
       shifter_1_out, shifter_2_out, subtractor_1_out;

  Demultiplexer #(.select(3), .width(8), .enable("false")) demultiplexer_1 (
    .out0(A_soma), .out1(A_Sub), .out2(A_Mult), .out3(A_Div), .out4(A_Neg), .out5(A_Comp), .out6(A_ShiftEsq),
    .out7(A_ShiftDir), .in(A), .sel(\Função ));
  Demultiplexer #(.select(3), .width(8), .enable("false")) demultiplexer_2 (
    .out0(B_soma), .out1(B_Sub), .out2(B_Mult), .out3(B_Div), .out5(B_Comp), .in(B), .sel(\Função ));  // open: out4, out6, out7
  Adder adder_1 (.a(A_soma), .b(B_soma), .out(adder_1_out));  // open: cin, cout
  Subtractor subtractor_1 (.a(A_Sub), .b(B_Sub), .out(subtractor_1_out));  // open: bin, bout
  Multiplier multiplier_1 (.a(A_Mult), .b(B_Mult), .out(multiplier_1_out));  // open: cin, cout
  Divider divider_1 (.a(A_Div), .b(B_Div), .out(divider_1_out));  // open: upper, rem
  Negator negator_1 (.in(A_Neg), .out(negator_1_out));
  Comparator comparator_1 (.a(A_Comp), .b(B_Comp), .eq(IGUAL), .lt(comparator_1_lt));  // open: gt
  Shifter shifter_1 (.in(A_ShiftEsq), .\dist (Shamt), .out(shifter_1_out));
  Shifter #(.shift("lr")) shifter_2 (.in(A_ShiftDir), .\dist (Shamt), .out(shifter_2_out));
  assign bit_extender_1_out = {{7{1'b0}}, comparator_1_lt};  // Bit_Extender bit_extender_1
  Multiplexer #(.select(3), .width(8), .enable("false")) multiplexer_1 (
    .in0(adder_1_out), .in1(subtractor_1_out), .in2(multiplier_1_out), .in3(divider_1_out),
    .in4(negator_1_out), .in5(bit_extender_1_out), .in6(shifter_1_out), .in7(shifter_2_out), .out(Resultado),
    .sel(\Função ));
endmodule

module unidade_de_controle (
  input  [2:0] opcode,
  output RegDst,
  output RegWrite,
  output ALUSrc,
  output MemWrite,
  output MemRead,
  output MemToReg,
  output Branch,
  output Jump,
  output [1:0] ALUOp
);

  wire and_1_out, and_4_out, and_5_out, and_8_out, and_9_out, nor_2_out;

  nor nor_1 (RegDst, opcode[1], opcode[1], opcode[2]);
  nor nor_2 (nor_2_out, opcode[1], opcode[2]);
  and and_1 (and_1_out, ~opcode[1], ~opcode[1], opcode[2]);  // AND_Gate
  ExactlyOne xor_1 (.out(ALUSrc), .in0(opcode[1]), .in1(opcode[1]), .in2(opcode[2]));
  and and_2 (MemWrite, ~opcode[1], opcode[1], ~opcode[2]);  // AND_Gate
  and and_3 (MemRead, opcode[1], ~opcode[1], ~opcode[2]);  // AND_Gate
  and and_4 (and_4_out, ~opcode[1], ~opcode[1], ~opcode[2]);  // AND_Gate
  and and_5 (and_5_out, ~opcode[1], ~opcode[1], opcode[2]);  // AND_Gate
  and and_6 (Branch, opcode[1], opcode[1], ~opcode[2]);  // AND_Gate
  and and_7 (Jump, opcode[1], opcode[1], opcode[2]);
  and and_8 (and_8_out, opcode[1], opcode[1], ~opcode[2]);  // AND_Gate
  and and_9 (and_9_out, ~opcode[1], ~opcode[1], opcode[2]);  // AND_Gate
  and and_10 (ALUOp[1], ~opcode[1], ~opcode[1]);  // AND_Gate
  or or_1 (RegWrite, nor_2_out, and_1_out);
  or or_2 (MemToReg, and_4_out, and_5_out);
  or or_3 (ALUOp[0], and_8_out, and_9_out);

  assign opcode[0] = opcode[1];
endmodule

module Controle_ULA (
  input  [2:0] FuncT,
  input  [1:0] ALUOp,
  output [2:0] ULACtrl
);

  Multiplexer #(.select(2), .width(3), .enable("false")) multiplexer_1 (
    .in0(3'b000), .in1(3'b101), .in2(FuncT), .in3(3'b000), .out(ULACtrl), .sel(ALUOp));
endmodule
